# Fritzing sketch Untitled Sketch (saved by Fritzing 0.9.4)
breadboards: 1

parts:
  Arduino_Nano = Arduino Nano (Rev3.0)
  HX711_module = HX711 Weighing Sensor Module
  12V_in = Power plug
  U1 = Voltage Regulator - 5V [package="TO220 [THT]"]
  C1 = Electrolytic Capacitor [capacitance=10µF package="100 mil [THT, electrolytic]"]
  C2 = Electrolytic Capacitor [capacitance=10µF package="100 mil [THT, electrolytic]"]
  Resin_Button = Toggle Switch [package=THT]
  Hardener_Button = Toggle Switch [package=THT]
  Reset_button = Toggle Switch [package=THT]
  Resin_Relay = Relay [part_number=FRS1B-S package=THT]
  Hardener_Relay = Relay [part_number=FRS1B-S package=THT]
  To_resin_solenoid = Camdenboss CTB0158-2 [package=THT]
  To_hardener_solenoid = Camdenboss CTB0158-2 [package=THT]
  To_Load_Cell = Camdenboss CTB0158-4 [part_number=CTB0158-4 package=THT]
  R1 = Resistor [tolerance=±5% resistance=1k package=THT]
  R2 = Resistor [tolerance=±5% resistance=1k package=THT]
  R3 = Resistor [tolerance=±5% resistance=1k package=THT]
  Resin_LED = LED - 5mm [color="Red (633nm)" package="5 mm [THT]"]
  Hardener_LED = LED - 5mm [color="Red (633nm)" package="5 mm [THT]"]
  R4 = Resistor [tolerance=±5% resistance=330 package=THT]
  R5 = Resistor [tolerance=±5% resistance=330 package=THT]
  D1 = Rectifier Diode [part_number=1N4001 package="300 mil [THT]"]
  D2 = Rectifier Diode [part_number=1N4001 package="300 mil [THT]"]
  D3 = Rectifier Diode [part_number=1N4001 package="300 mil [THT]"]
  D4 = Rectifier Diode [part_number=1N4001 package="300 mil [THT]"]
  Clean_Button = Toggle Switch [package=THT]
  R6 = Resistor [tolerance=±5% resistance=1k package=THT]

nets:
  GND: Arduino_Nano.GND, HX711_module.GND, 12V_in.GND, U1.GND, C1.-, C2.-, Resin_Relay.COIL1, Hardener_Relay.COIL1, To_resin_solenoid.pin2, To_hardener_solenoid.pin2, R1.Pin_1, R2.Pin_1, R3.Pin_1, Resin_LED.cathode, Hardener_LED.cathode, D1.anode, D2.anode, D3.anode, D4.anode, R6.Pin_1
  N1: Arduino_Nano.D2, Hardener_Relay.COIL2, D3.cathode
  N2: Arduino_Nano.D3, Resin_Button.COM, R1.Pin_0
  N3: Arduino_Nano.D4, Hardener_Button.COM, R2.Pin_0
  N4: Arduino_Nano.D5, Reset_button.COM, R3.Pin_0
  N5: Arduino_Nano.D8, R4.Pin_0
  N6: Arduino_Nano.D10, R5.Pin_0
  N7: Arduino_Nano.D11/MOSI, Resin_Relay.COIL2, D4.cathode
  N8: Arduino_Nano.D12/MISO, Clean_Button.COM, R6.Pin_0
  5V: Arduino_Nano.5V, HX711_module.VCC, U1.output_voltage, C2.+, Resin_Button.L1, Hardener_Button.L1, Reset_button.L2, Clean_Button.L2
  N9: Arduino_Nano.A1, HX711_module.DO/RX
  N10: Arduino_Nano.A0, HX711_module.CK/TX
  N11: HX711_module.E+, To_Load_Cell.pin4
  N12: HX711_module.E-, To_Load_Cell.pin3
  N13: HX711_module.A+, To_Load_Cell.pin1
  N14: HX711_module.A-, To_Load_Cell.pin2
  12V: 12V_in.VCC, U1.input_voltage, C1.+, Resin_Relay.A, Hardener_Relay.A
  N15: Resin_Relay.C1, Resin_Relay.C2, To_resin_solenoid.pin1, D2.cathode
  N16: Hardener_Relay.C1, Hardener_Relay.C2, To_hardener_solenoid.pin1, D1.cathode
  N17: Resin_LED.anode, R4.Pin_1
  N18: Hardener_LED.anode, R5.Pin_1
